# Fritzing sketch Doser (saved by Fritzing 0.9.3b)
breadboards: 2

parts:
  Part1 = Arduino Uno (Rev3)
  Power_plug1 = Power plug [part_number="12v dc"]
  LM1 = RioRand LM2596
  U1 = 74HC595 SMD [package="SO16 [SMD]"]
  IRLZ44N_8 = Basic FET N-Channel [part_number="IRLZ44N " package="TO220 [THT]"]
  IRLZ44N_6 = Basic FET N-Channel [part_number="IRLZ44N " package="TO220 [THT]"]
  IRLZ44N_5 = Basic FET N-Channel [part_number="IRLZ44N " package="TO220 [THT]"]
  IRLZ44N_4 = Basic FET N-Channel [part_number="IRLZ44N " package="TO220 [THT]"]
  IRLZ44N_3 = Basic FET N-Channel [part_number="IRLZ44N " package="TO220 [THT]"]
  1N4001_8 = Diode [package=diode-1n4001]
  Motor_8 = DC Motor [part_number="12V 80mA"]
  IRLZ44N_7 = Basic FET N-Channel [part_number="IRLZ44N " package="TO220 [THT]"]
  1N4001_7 = Diode [package=diode-1n4001]
  Motor_7 = DC Motor [part_number="12V 80mA"]
  Motor_6 = DC Motor [part_number="12V 80mA"]
  1N4001_6 = Diode [package=diode-1n4001]
  IRLZ44N_2 = Basic FET N-Channel [part_number="IRLZ44N " package="TO220 [THT]"]
  IRLZ44N_1 = Basic FET N-Channel [part_number="IRLZ44N " package="TO220 [THT]"]
  1N4001_5 = Diode [package=diode-1n4001]
  1N4001_4 = Diode [package=diode-1n4001]
  1N4001_3 = Diode [package=diode-1n4001]
  1N4001_2 = Diode [package=diode-1n4001]
  1N4001_1 = Diode [package=diode-1n4001]
  Motor_5 = DC Motor [part_number="12V 80mA"]
  Motor_4 = DC Motor [part_number="12V 80mA"]
  Motor_1 = DC Motor [part_number="12V 80mA"]
  Motor_3 = DC Motor [part_number="12V 80mA"]
  Motor_9 = DC Motor [part_number="12V 80mA"]

nets:
  N1: Part1.D8, U1.Q6, U1.SH_CP, IRLZ44N_6.gate
  N2: Part1.D9_PWM, U1.Q5, U1.ST_CP, IRLZ44N_7.gate
  N3: Part1.D10_PWM/SS, U1.Q3, U1.DS, IRLZ44N_4.gate
  N4: Part1.GND, LM1.Pin_3
  N5: Part1.VIN, LM1.Pin_2
  N6: Power_plug1.GND, LM1.Pin_1, U1.Q4, U1.OE, IRLZ44N_8.source, IRLZ44N_6.source, IRLZ44N_5.gate, IRLZ44N_5.source, IRLZ44N_4.source, IRLZ44N_3.source, IRLZ44N_7.source, IRLZ44N_2.source, IRLZ44N_1.source
  VCC: Power_plug1.VCC, LM1.Pin_0, U1.Q1, U1.Q7, U1.MR, U1.VCC, IRLZ44N_8.gate, 1N4001_8.C, Motor_8.pin_2, 1N4001_7.C, Motor_7.pin_2, Motor_6.pin_2, 1N4001_6.C, IRLZ44N_2.gate, 1N4001_5.C, 1N4001_4.C, 1N4001_3.C, 1N4001_2.C, 1N4001_1.C, Motor_5.pin_2, Motor_4.pin_2, Motor_1.pin_2, Motor_3.pin_2, Motor_9.pin_2
  N7: U1.Q2, U1.Q0, IRLZ44N_3.gate, IRLZ44N_1.gate
  N8: U1.GND, U1.Q7'
  N9: IRLZ44N_8.drain, 1N4001_8.A, Motor_8.pin_1
  N10: IRLZ44N_6.drain, Motor_6.pin_1, 1N4001_6.A
  N11: IRLZ44N_5.drain, 1N4001_5.A, Motor_5.pin_1
  N12: IRLZ44N_4.drain, 1N4001_4.A, Motor_4.pin_1
  N13: IRLZ44N_3.drain, 1N4001_3.A, Motor_3.pin_1
  N14: IRLZ44N_7.drain, 1N4001_7.A, Motor_7.pin_1
  N15: IRLZ44N_2.drain, 1N4001_2.A, Motor_9.pin_1
  N16: IRLZ44N_1.drain, 1N4001_1.A, Motor_1.pin_1

notes:
  Wifi ESP-01
  Step Down
  5V 2A
  12V DC 2A Outlet
  SD Card
  RTC
  Display
  + -
  12V 80mA
  1N4001
  IRLZ44N
