# Fritzing sketch Grow (saved by Fritzing 0.9.3b)
breadboards: 1

parts:
  Part1 = Arduino Uno (Rev3)
  RHT1 = Humidity and Temperature Sensor RHT03
  R1 = Resistor [tolerance=±0.1% resistance=10k package=THT]
  R2 = Photocell (LDR) [package=THT]
  R3 = Resistor [tolerance=±5% resistance=10k package=THT]

nets:
  N1: Part1.A0, R2.pin_0, R3.Pin_1
  N2: Part1.D2, RHT1.Data-signal, R1.Pin_0
  5V: Part1.5V, RHT1.Vcc, R1.Pin_1, R2.pin_1
  N3: Part1.GND, RHT1.GND_2, R3.Pin_0
